// Logisim project WITCPU.circ as structural Verilog: 6 circuits, main circuit main
module main (
);

  wire and_1_out, and_2_out, bus_controller_1_alu, bus_controller_1_ram_read, bus_controller_1_ram_write,
       bus_controller_1_reg_write, Clock_out, Cycle_q, not_1_out;
  wire [3:0] decoder_1_opcode, decoder_1_rd_op1, decoder_1_rx_op2, decoder_1_ry_op3;
  wire [7:0] bus_controller_1_address, decoder_1_imm, multiplexer_1_out, pc_controller_1_output, pc_q;
  wire [15:0] alu_1_output, Instruction_q, register_1_x, register_1_y;

  Clock Clock (.out(Clock_out));
  Decoder decoder_1 (
    .instruct_input(Instruction_q), .ry_op3(decoder_1_ry_op3), .rx_op2(decoder_1_rx_op2),
    .rd_op1(decoder_1_rd_op1), .opcode(decoder_1_opcode), .imm(decoder_1_imm));
  not not_1 (not_1_out, Clock_out);
  T_Flip_Flop Cycle (.clk(not_1_out), .T(1'b1), .Q(Cycle_q));  // open: Qn, preset, reset, en
  Bus_Controller bus_controller_1 (
    .clock(Clock_out), .cycle(Cycle_q), .opcode(decoder_1_opcode), .imm(decoder_1_imm), .data(register_1_x),
    .ALU(bus_controller_1_alu), .reg_write(bus_controller_1_reg_write), .RAM_read(bus_controller_1_ram_read),
    .RAM_write(bus_controller_1_ram_write), .Address(bus_controller_1_address));
  Register register_1 (
    .data(alu_1_output), .clock_input(bus_controller_1_reg_write), .rd(decoder_1_rd_op1), .X(register_1_x),
    .rx(decoder_1_rx_op2), .Y(register_1_y), .ry(decoder_1_ry_op3));
  PC_Controller pc_controller_1 (
    .pre_pc(pc_q), .imm(decoder_1_imm), .data(register_1_x), .opcode(decoder_1_opcode),
    .\output (pc_controller_1_output));
  ALU alu_1 (
    .X(register_1_x), .Y(register_1_y), .imm_input(decoder_1_imm), .alu_clock(bus_controller_1_alu),
    .\output (alu_1_output), .opcode_input(decoder_1_opcode));
  and and_1 (and_1_out, Clock_out, Cycle_q);
  and and_2 (and_2_out, Clock_out, ~Cycle_q);  // AND_Gate
  Register_part pc (.D(pc_controller_1_output), .Q(pc_q), .clk(and_1_out));  // open: en, clr
  Multiplexer #(.width(8)) multiplexer_1 (
    .in0(pc_q), .in1(bus_controller_1_address), .out(multiplexer_1_out), .sel(Cycle_q));  // open: en
  RAM #(.dataWidth(16), .bus("separate")) ram_1 (
    .addr(multiplexer_1_out), .din(register_1_x), .data(alu_1_output), .str(bus_controller_1_ram_write),
    .clk(Clock_out), .ld(bus_controller_1_ram_read));  // open: sel, clr
  Register_part #(.width(16)) Instruction (.D(alu_1_output), .Q(Instruction_q), .clk(and_2_out));  // open: en, clr
endmodule

module ALU (
  input  [15:0] X,
  input  [15:0] Y,
  input  alu_clock,
  input  [3:0] opcode_input,
  input  [7:0] imm_input,
  output [15:0] \output 
);

  wire [15:0] adder_1_out, and_1_out, divider_1_out, multiplexer_1_out, multiplier_1_out, or_1_out,
       subtractor_1_out, xnor_1_out;

  assign and_1_out = X & Y;  // AND_Gate and_1, 16 bits wide
  assign or_1_out = X | Y;  // OR_Gate or_1, 16 bits wide
  Adder #(.width(16)) adder_1 (.a(X), .b(Y), .out(adder_1_out));  // open: cin, cout
  Subtractor #(.width(16)) subtractor_1 (.a(X), .b(Y), .out(subtractor_1_out));  // open: bin, bout
  Multiplier #(.width(16)) multiplier_1 (.a(X), .b(Y), .out(multiplier_1_out));  // open: cin, cout
  Divider #(.width(16)) divider_1 (.a(X), .b(Y), .out(divider_1_out));  // open: upper, rem
  assign xnor_1_out = ~(X ^ Y);  // XNOR_Gate xnor_1, 16 bits wide
  Multiplexer #(.select(3), .width(16)) multiplexer_1 (
    .in0(adder_1_out), .in1(subtractor_1_out), .in2(multiplier_1_out), .in3(divider_1_out), .in4(and_1_out),
    .in5(or_1_out), .in6(xnor_1_out), .in7({{9{imm_input[7]}}, imm_input[6:0]}), .out(multiplexer_1_out),
    .sel(opcode_input[2:0]));  // open: en
  assign \output  = alu_clock ? multiplexer_1_out : 16'bz;  // Controlled_Buffer controlled_buffer_1
endmodule

// BC
module Bus_Controller (
  input  clock,
  input  cycle,
  input  [3:0] opcode,
  input  [7:0] imm,
  input  [15:0] data,
  output ALU,
  output reg_write,
  output RAM_read,
  output RAM_write,
  output [7:0] Address
);

  wire and_1_out, or_1_out;

  and and_1 (and_1_out, ~opcode[1], opcode[2], opcode[3]);  // AND_Gate
  and and_2 (ALU, cycle, ~opcode[3]);  // AND_Gate
  or or_1 (or_1_out, ~opcode[3], and_1_out);  // OR_Gate
  and and_3 (reg_write, clock, cycle, or_1_out);
  or or_2 (RAM_read, ~cycle, and_1_out);  // OR_Gate
  Multiplexer #(.width(8)) multiplexer_1 (.in0(imm), .in1(data[7:0]), .out(Address), .sel(opcode[0]));  // open: en
  and and_4 (RAM_write, cycle, opcode[1], opcode[2], opcode[3]);
endmodule

module Decoder (
  input  [15:0] instruct_input,
  output [3:0] ry_op3,
  output [3:0] rx_op2,
  output [3:0] rd_op1,
  output [3:0] opcode,
  output [7:0] imm
);


  assign imm = instruct_input[7:0];
  assign opcode = instruct_input[15:12];
  assign rd_op1 = instruct_input[11:8];
  assign rx_op2 = instruct_input[7:4];
  assign ry_op3 = instruct_input[3:0];
endmodule

// PC
module PC_Controller (
  input  [7:0] pre_pc,
  input  [7:0] imm,
  input  [15:0] data,
  input  [3:0] opcode,
  output [7:0] \output 
);

  wire and_1_out, comparator_1_eq, comparator_1_gt, comparator_1_lt, multiplexer_1_out, not_1_out;
  wire [7:0] adder_1_out;

  Comparator #(.width(16)) comparator_1 (
    .a(data), .b({16{1'b0}}), .gt(comparator_1_gt), .eq(comparator_1_eq), .lt(comparator_1_lt));
  Adder adder_1 (.a(pre_pc), .b(8'h1), .out(adder_1_out));  // open: cin, cout
  not not_1 (not_1_out, comparator_1_eq);
  Multiplexer #(.select(2)) multiplexer_1 (
    .in0(comparator_1_eq), .in1(not_1_out), .in2(comparator_1_gt), .in3(comparator_1_lt),
    .out(multiplexer_1_out), .sel(opcode[1:0]));  // open: en
  and and_1 (and_1_out, multiplexer_1_out, ~opcode[2], opcode[3]);  // AND_Gate
  Multiplexer #(.width(8)) multiplexer_2 (.in0(adder_1_out), .in1(imm), .out(\output ), .sel(and_1_out));  // open: en
endmodule

// Reg
module Register (
  input  [15:0] data,
  input  [3:0] rx,
  input  clock_input,
  input  [3:0] rd,
  input  [3:0] ry,
  output [15:0] X,
  output [15:0] Y
);

  wire demultiplexer_1_out0, demultiplexer_1_out1, demultiplexer_1_out2, demultiplexer_1_out3,
       demultiplexer_1_out4, demultiplexer_1_out5, demultiplexer_1_out6, demultiplexer_1_out7,
       demultiplexer_1_out8, demultiplexer_1_out9, demultiplexer_1_out10, demultiplexer_1_out11,
       demultiplexer_1_out12, demultiplexer_1_out13, demultiplexer_1_out14, demultiplexer_1_out15;
  wire [15:0] R0_q, R1_q, R2_q, R3_q, R4_q, R5_q, R6_q, R7_q, R8_q, R9_q, Ra_q, Rb_q, Rc_q, Rd_q, Re_q, Rf_q;

  Demultiplexer #(.select(4)) demultiplexer_1 (
    .out0(demultiplexer_1_out0), .out1(demultiplexer_1_out1), .out2(demultiplexer_1_out2),
    .out3(demultiplexer_1_out3), .out4(demultiplexer_1_out4), .out5(demultiplexer_1_out5),
    .out6(demultiplexer_1_out6), .out7(demultiplexer_1_out7), .out8(demultiplexer_1_out8),
    .out9(demultiplexer_1_out9), .out10(demultiplexer_1_out10), .out11(demultiplexer_1_out11),
    .out12(demultiplexer_1_out12), .out13(demultiplexer_1_out13), .out14(demultiplexer_1_out14),
    .out15(demultiplexer_1_out15), .in(clock_input), .sel(rd));  // open: en
  Register_part #(.width(16)) R0 (.D({16{1'b0}}), .Q(R0_q), .clk(demultiplexer_1_out0));  // open: en, clr
  Register_part #(.width(16)) R3 (.D(data), .Q(R3_q), .clk(demultiplexer_1_out3));  // open: en, clr
  Register_part #(.width(16)) R6 (.D(data), .Q(R6_q), .clk(demultiplexer_1_out6));  // open: en, clr
  Register_part #(.width(16)) R9 (.D(data), .Q(R9_q), .clk(demultiplexer_1_out9));  // open: en, clr
  Register_part #(.width(16)) Rc (.D(data), .Q(Rc_q), .clk(demultiplexer_1_out12));  // open: en, clr
  Register_part #(.width(16)) R1 (.D(data), .Q(R1_q), .clk(demultiplexer_1_out1));  // open: en, clr
  Register_part #(.width(16)) R4 (.D(data), .Q(R4_q), .clk(demultiplexer_1_out4));  // open: en, clr
  Register_part #(.width(16)) R7 (.D(data), .Q(R7_q), .clk(demultiplexer_1_out7));  // open: en, clr
  Register_part #(.width(16)) Ra (.D(data), .Q(Ra_q), .clk(demultiplexer_1_out10));  // open: en, clr
  Register_part #(.width(16)) u_Rd (.D(data), .Q(Rd_q), .clk(demultiplexer_1_out13));  // open: en, clr
  Register_part #(.width(16)) R2 (.D(data), .Q(R2_q), .clk(demultiplexer_1_out2));  // open: en, clr
  Register_part #(.width(16)) R5 (.D(data), .Q(R5_q), .clk(demultiplexer_1_out5));  // open: en, clr
  Register_part #(.width(16)) R8 (.D(data), .Q(R8_q), .clk(demultiplexer_1_out8));  // open: en, clr
  Register_part #(.width(16)) Rb (.D(data), .Q(Rb_q), .clk(demultiplexer_1_out11));  // open: en, clr
  Register_part #(.width(16)) Re (.D(data), .Q(Re_q), .clk(demultiplexer_1_out14));  // open: en, clr
  Register_part #(.width(16)) Rf (.D(data), .Q(Rf_q), .clk(demultiplexer_1_out15));  // open: en, clr
  Multiplexer #(.select(4), .width(16)) multiplexer_1 (
    .in0(R0_q), .in1(R1_q), .in2(R2_q), .in3(R3_q), .in4(R4_q), .in5(R5_q), .in6(R6_q), .in7(R7_q),
    .in8(R8_q), .in9(R9_q), .in10(Ra_q), .in11(Rb_q), .in12(Rc_q), .in13(Rd_q), .in14(Re_q), .in15(Rf_q),
    .out(X), .sel(rx));  // open: en
  Multiplexer #(.select(4), .width(16)) multiplexer_2 (
    .in0(R0_q), .in1(R1_q), .in2(R2_q), .in3(R3_q), .in4(R4_q), .in5(R5_q), .in6(R6_q), .in7(R8_q),
    .in8(R8_q), .in9(R9_q), .in10(Ra_q), .in11(Rb_q), .in12(Rc_q), .in13(Rd_q), .in14(Re_q), .in15(Rf_q),
    .out(Y), .sel(ry));  // open: en
endmodule
