// Logisim project lab4.circ as structural Verilog: 1 circuit, main circuit main
module main (
  output OUTPUT
);

  wire and_2_out, and_3_out, and_4_out, and_5_out, and_6_out, and_7_out, and_8_out, CABBAGE_q, CABBAGE_qn,
       FARMER_q, FARMER_qn, GOAT_q, GOAT_qn, INPUT_out, or_1_out, or_2_out, or_3_out, WOLF_q, WOLF_qn;

  Clock INPUT (.out(INPUT_out));
  and and_1 (OUTPUT, FARMER_q, CABBAGE_q, GOAT_q, WOLF_q);
  D_Flip_Flop WOLF (.clk(INPUT_out), .D(or_2_out), .Q(WOLF_q), .Qn(WOLF_qn));  // open: preset, en, reset
  D_Flip_Flop GOAT (.clk(INPUT_out), .D(or_1_out), .Q(GOAT_q), .Qn(GOAT_qn));  // open: preset, en, reset
  D_Flip_Flop CABBAGE (.clk(INPUT_out), .D(or_3_out), .Q(CABBAGE_q), .Qn(CABBAGE_qn));  // open: preset, en, reset
  T_Flip_Flop FARMER (.clk(INPUT_out), .T(1'b1), .Q(FARMER_q), .Qn(FARMER_qn));  // open: preset, reset, en
  and and_2 (and_2_out, WOLF_q, GOAT_qn, CABBAGE_q, FARMER_qn);
  and and_3 (and_3_out, WOLF_q, GOAT_qn, CABBAGE_q, FARMER_q);
  and and_4 (and_4_out, WOLF_q, GOAT_qn, CABBAGE_qn, FARMER_qn);
  and and_5 (and_5_out, WOLF_q, GOAT_q, CABBAGE_qn, FARMER_q);
  and and_6 (and_6_out, WOLF_qn, GOAT_q, CABBAGE_qn, FARMER_qn);
  and and_7 (and_7_out, WOLF_qn, GOAT_q, CABBAGE_qn, FARMER_q);
  and and_8 (and_8_out, WOLF_qn, GOAT_qn, CABBAGE_qn, FARMER_qn);
  or or_1 (or_1_out, and_8_out, and_7_out, and_2_out, and_6_out);
  or or_2 (or_2_out, and_6_out, and_5_out, and_2_out, and_4_out, and_3_out);
  or or_3 (or_3_out, and_4_out, and_2_out, and_3_out);
endmodule
